// Digital circuit DRAM.dig as structural Verilog
module DRAM (
  input  [3:0] Address_bits,
  input  Clock,
  input  [1:0] Clear_Store_Load,
  input  [3:0] Data_input,
  output [3:0] Output_databus
);

  wire and_1_out, decoder_1_out_0, decoder_1_out_1, decoder_1_out_2, decoder_1_out_3, decoder_1_out_4,
       decoder_1_out_5, decoder_1_out_6, decoder_1_out_7, decoder_1_out_8, decoder_1_out_9, decoder_1_out_10,
       decoder_1_out_11, decoder_1_out_12, decoder_1_out_13, decoder_1_out_14, decoder_1_out_15;
  wire [3:0] Row_0_p4, Row_1_p3, Row_2_p3, Row_3_p3, Row_4_p3, Row_5_p3, Row_6_p3, Row_7_p3, Row_8_p3,
       Row_9_p3, Row_10_p3, Row_11_p3, Row_12_p3, Row_13_p3, Row_14_p3, Row_15_p3;

  Decoder #(.Selector_Bits(4)) decoder_1 (
    .sel(Address_bits), .out_0(decoder_1_out_0), .out_1(decoder_1_out_1), .out_2(decoder_1_out_2),
    .out_3(decoder_1_out_3), .out_4(decoder_1_out_4), .out_5(decoder_1_out_5), .out_6(decoder_1_out_6),
    .out_7(decoder_1_out_7), .out_8(decoder_1_out_8), .out_9(decoder_1_out_9), .out_10(decoder_1_out_10),
    .out_11(decoder_1_out_11), .out_12(decoder_1_out_12), .out_13(decoder_1_out_13),
    .out_14(decoder_1_out_14), .out_15(decoder_1_out_15));
  and and_1 (and_1_out, decoder_1_out_0, Clock);
  // And and_2 has open pins: In_1=decoder_1_out_6, In_2=Clock, out=open
  // And and_3 has open pins: In_1=decoder_1_out_11, In_2=Clock, out=open
  // storeclear Row_0: pin names not known; wires that end beside it: and_1_out, Data_input, Clear_Store_Load, Row_0_p4
  // storeclear Row_6: pin names not known; wires that end beside it: Data_input, Clear_Store_Load, Row_6_p3
  // storeclear Row_11: pin names not known; wires that end beside it: Data_input, Clear_Store_Load, Row_11_p3
  // And and_4 has open pins: In_1=decoder_1_out_1, In_2=Clock, out=open
  // And and_5 has open pins: In_1=decoder_1_out_7, In_2=Clock, out=open
  // And and_6 has open pins: In_1=decoder_1_out_12, In_2=Clock, out=open
  // storeclear Row_1: pin names not known; wires that end beside it: Data_input, Clear_Store_Load, Row_1_p3
  // storeclear Row_7: pin names not known; wires that end beside it: Data_input, Clear_Store_Load, Row_7_p3
  // storeclear Row_12: pin names not known; wires that end beside it: Data_input, Clear_Store_Load, Row_12_p3
  // And and_7 has open pins: In_1=decoder_1_out_2, In_2=Clock, out=open
  // And and_8 has open pins: In_1=decoder_1_out_8, In_2=Clock, out=open
  // And and_9 has open pins: In_1=decoder_1_out_13, In_2=Clock, out=open
  // storeclear Row_2: pin names not known; wires that end beside it: Data_input, Clear_Store_Load, Row_2_p3
  // storeclear Row_8: pin names not known; wires that end beside it: Data_input, Clear_Store_Load, Row_8_p3
  // storeclear Row_13: pin names not known; wires that end beside it: Data_input, Clear_Store_Load, Row_13_p3
  // And and_10 has open pins: In_1=decoder_1_out_3, In_2=Clock, out=open
  // And and_11 has open pins: In_1=decoder_1_out_9, In_2=Clock, out=open
  // And and_12 has open pins: In_1=decoder_1_out_14, In_2=Clock, out=open
  // storeclear Row_3: pin names not known; wires that end beside it: Data_input, Clear_Store_Load, Row_3_p3
  // storeclear Row_9: pin names not known; wires that end beside it: Data_input, Clear_Store_Load, Row_9_p3
  // storeclear Row_14: pin names not known; wires that end beside it: Data_input, Clear_Store_Load, Row_14_p3
  // And and_13 has open pins: In_1=decoder_1_out_4, In_2=Clock, out=open
  // And and_14 has open pins: In_1=decoder_1_out_10, In_2=Clock, out=open
  // And and_15 has open pins: In_1=decoder_1_out_15, In_2=Clock, out=open
  // storeclear Row_4: pin names not known; wires that end beside it: Data_input, Clear_Store_Load, Row_4_p3
  // storeclear Row_10: pin names not known; wires that end beside it: Data_input, Clear_Store_Load, Row_10_p3
  // storeclear Row_15: pin names not known; wires that end beside it: Data_input, Clear_Store_Load, Row_15_p3
  // And and_16 has open pins: In_1=decoder_1_out_5, In_2=Clock, out=open
  // storeclear Row_5: pin names not known; wires that end beside it: Data_input, Clear_Store_Load, Row_5_p3
  Multiplexer #(.Bits(4), .Selector_Bits(4)) multiplexer_1 (
    .sel(Address_bits), .in_0(Row_0_p4), .in_1(Row_1_p3), .in_2(Row_2_p3), .in_3(Row_3_p3), .in_4(Row_4_p3),
    .in_5(Row_5_p3), .in_6(Row_6_p3), .in_7(Row_7_p3), .in_8(Row_8_p3), .in_9(Row_9_p3), .in_10(Row_10_p3),
    .in_11(Row_11_p3), .in_12(Row_12_p3), .in_13(Row_13_p3), .in_14(Row_14_p3), .in_15(Row_15_p3),
    .out(Output_databus));

  // Notes on the sheet:
  //   Clear_Store_Load: 0 -> clear
  //   1 -> store
  //   2 -> load
  //   F -> empty
endmodule
