// Digital circuit controltype.dig as structural Verilog
module controltype (
  input  C,
  output IR_HI_Write,
  output IR_LO_Write,
  output [4:0] States,
  output WriteBack,
  output Increment
);

  D_FF IF1 (.D(States[4]), .C(C), .Q(IR_HI_Write));  // open: nQ
  D_FF IF2 (.D(IR_HI_Write), .C(C), .Q(IR_LO_Write));  // open: nQ
  D_FF Decode (.D(IR_LO_Write), .C(C), .Q(States[2]));  // open: nQ
  D_FF Execute (.D(States[2]), .C(C), .Q(States[3]));  // open: nQ
  or or_1 (Increment, IR_HI_Write, States[4]);
  D_FF u_WriteBack (.D(States[3]), .C(C), .Q(States[4]));  // open: nQ

  assign States[1:0] = {IR_LO_Write, IR_HI_Write};
  assign WriteBack = States[4];
endmodule
