// Digital circuit register files.dig as structural Verilog
module register_files (
  input  clock,
  input  [1:0] ReadRegister1,
  input  [1:0] ReadRegister2,
  input  [7:0] control_signals,
  input  [3:0] Write_data,
  input  [1:0] Write_register,
  output [3:0] ReadData1,
  output [3:0] ReadData2
);

  wire [3:0] demultiplexer_1_out_0, demultiplexer_1_out_1, demultiplexer_1_out_2, demultiplexer_1_out_3,
       R0_p4, R1_p4, R2_p4, R3_p4;

  Demultiplexer #(.Bits(4), .Selector_Bits(2)) demultiplexer_1 (
    .sel(Write_register), .in(Write_data), .out_0(demultiplexer_1_out_0), .out_1(demultiplexer_1_out_1),
    .out_2(demultiplexer_1_out_2), .out_3(demultiplexer_1_out_3));
  // General_register R0: pin names not known; wires that end beside it: clock, demultiplexer_1_out_0, control_signals[1:0], R0_p4
  // General_register R1: pin names not known; wires that end beside it: clock, demultiplexer_1_out_1, control_signals[3:2], R1_p4
  // General_register R2: pin names not known; wires that end beside it: clock, demultiplexer_1_out_2, control_signals[5:4], R2_p4
  // General_register R3: pin names not known; wires that end beside it: clock, demultiplexer_1_out_3, control_signals[7:6], R3_p4
  Multiplexer #(.Bits(4), .Selector_Bits(2)) multiplexer_1 (
    .sel(ReadRegister1), .in_0(R0_p4), .in_1(R1_p4), .in_2(R2_p4), .in_3(R3_p4), .out(ReadData1));
  Multiplexer #(.Selector_Bits(2), .Bits(4)) multiplexer_2 (
    .sel(ReadRegister2), .in_0(R0_p4), .in_1(R1_p4), .in_2(R2_p4), .in_3(R3_p4), .out(ReadData2));
endmodule
